# Fritzing sketch tiny_minipro (saved by Fritzing 0.9.3b)

parts:
  Digispark1 = Digispark
  Part1 = Arduino Pro Mini v13

nets:
  VCC: Digispark1.VCC, Part1.VCC
  GND: Digispark1.GND, Part1.GND
  N1: Digispark1.P0, Part1.D11_PWM/MOSI
  N2: Digispark1.P1, Part1.D12/MISO
  N3: Digispark1.P2, Part1.D13/SCK
  N4: Digispark1.P5, Part1.RESET

custom parts:
  Digispark: The Digispark is an Attiny85 based microcontroller development board similar to the Arduino line, only cheaper, smaller, and a bit less powerful. With a whole host of shields to extend its functionality and the ability to use the familiar Arduino IDE the Digispark is a great way to jump into electronics, or perfect for when an Arduino is too big or too much.
